# Fritzing sketch wiringPi-LED-Pin0 (saved by Fritzing 0.9.2b)
breadboards: 1

parts:
  LED1 = smd LED [color="Red (633nm)" package="0603 [SMD]"]
  R1 = Resistor [tolerance=±5% resistance=220 package="1206 [SMD]"]
  Raspberry_Pi1 = Raspberry Pi 2

nets:
  N1: LED1.cathode, R1.Pin_1
  N2: LED1.anode, Raspberry_Pi1.GPIO17
  N3: R1.Pin_0, Raspberry_Pi1.GND
