# Fritzing sketch rpi-levelshifter-neopixel (saved by Fritzing 0.9.2b)
breadboards: 1

parts:
  Raspberry_Pi1 = Raspberry Pi 2
  BB1 = 4-Line Bi-Directional Level Shifter
  NEOPIXEL3 = Neopixel Strip -- White (30/m)
  JACK1 = 2.1mm Barrel Jack with Terminal Block

nets:
  N1: Raspberry_Pi1.3v3, BB1.LV
  N2: Raspberry_Pi1.GPIO18, BB1.A1
  GND: Raspberry_Pi1.GND, BB1.GND, NEOPIXEL3.GND, JACK1.NEG
  N3: BB1.HV, NEOPIXEL3.+5V, JACK1.POS
  N4: BB1.B1, NEOPIXEL3.Din

custom parts:
  4-Line Bi-Directional Level Shifter: 4-Channel Bi-Directional Level Shifter
  Neopixel Strip -- White (30/m): These NeoPixel strips have 30 digitally-addressable pixel LEDs per meter and are very affordable and are only 12.5 mm wide, 10 mm if you remove the strip from the casing.
