# Fritzing sketch traffic-light (saved by Fritzing 0.9.2b)
breadboards: 1

parts:
  Raspberry_Pi_1 = Raspberry Pi 3
  J2 = T Cobbler Plus
  R1 = Resistor [tolerance=±5% resistance=220 package="1206 [SMD]"]
  R2 = Resistor [tolerance=±5% resistance=220 package="1206 [SMD]"]
  R3 = Resistor [tolerance=±5% resistance=220 package="1206 [SMD]"]
  R4 = Resistor [tolerance=±5% resistance=220 package="1206 [SMD]"]
  R5 = Resistor [tolerance=±5% resistance=220 package="1206 [SMD]"]
  R6 = Resistor [tolerance=±5% resistance=1k package="1206 [SMD]"]
  R7 = Resistor [tolerance=±5% resistance=10k package="1206 [SMD]"]
  S2 = Round Pushbutton
  LED1 = LED - 5mm [color="Red (633nm)" package="5 mm [THT]"]
  LED2 = LED - 5mm [color="Green (565nm)" package="5 mm [THT]"]
  LED3 = LED - 5mm [color="Yellow (592nm)" package="5 mm [THT]"]
  LED4 = LED - 5mm [color="Red (633nm)" package="5 mm [THT]"]
  LED5 = LED - 5mm [color="Green (565nm)" package="5 mm [THT]"]

nets:
  3V3: Raspberry_Pi_1.3v3, Raspberry_Pi_1.3V3, J2.3.3V#41, J2.3.3V#57
  N1: Raspberry_Pi_1.GPIO2, J2.GPIO_2
  N2: Raspberry_Pi_1.GPIO3, J2.GPIO_3
  N3: Raspberry_Pi_1.GIPO4, J2.GPIO_4
  N4: Raspberry_Pi_1.GND, J2.GND#46, J2.GND#49, J2.GND#54, J2.GND#60, J2.GND#65, J2.GND#70, J2.GND#74, J2.GND#79
  N5: Raspberry_Pi_1.GIPO17, J2.GPIO_17
  N6: Raspberry_Pi_1.GIPO27, J2.GPIO_27
  N7: Raspberry_Pi_1.GIPO22, J2.GPIO_22
  N8: Raspberry_Pi_1.GIPO10, J2.GPIO_10
  N9: Raspberry_Pi_1.GIPO9, J2.GPIO_9
  N10: Raspberry_Pi_1.GIPO11, J2.GPIO_11
  N11: Raspberry_Pi_1.ID_SD, J2.ID_SD
  N12: Raspberry_Pi_1.GIPO5, J2.GPIO_5
  N13: Raspberry_Pi_1.GIPO6, J2.GPIO_6
  N14: Raspberry_Pi_1.GIPO13, J2.GPIO_13
  N15: Raspberry_Pi_1.GIPO19, J2.GPIO_19
  N16: Raspberry_Pi_1.GIPO26, J2.GPIO_26
  N17: Raspberry_Pi_1.GIPO21, J2.GPIO_21
  N18: Raspberry_Pi_1.GIPO20, J2.GPIO_20
  N19: Raspberry_Pi_1.GIPO16, J2.GPIO_16
  N20: Raspberry_Pi_1.GIPO12, J2.GPIO_12
  N21: Raspberry_Pi_1.ID_SC, J2.ID_SC
  N22: Raspberry_Pi_1.GIPO7, J2.GPIO_7
  N23: Raspberry_Pi_1.GIPO8, J2.GPIO_8
  N24: Raspberry_Pi_1.GIPO25, J2.GPIO_25
  N25: Raspberry_Pi_1.GIPO24, J2.GPIO_24
  N26: Raspberry_Pi_1.GIPO23, J2.GPIO_23
  N27: Raspberry_Pi_1.GIPO18, J2.GPIO_18
  N28: Raspberry_Pi_1.GIPO15, J2.GPIO_15
  N29: Raspberry_Pi_1.GIPO14, J2.GPIO_14
  5V: Raspberry_Pi_1.5V, J2.5V
  N30: J2.3V3, R7.Pin_1
  N31: J2.#17, R1.Pin_1
  N32: J2.#27, R2.Pin_1
  N33: J2.GND#13, R6.Pin_0, LED1.cathode, LED2.cathode, LED3.cathode, LED4.cathode, LED5.cathode
  N34: J2.#22, R3.Pin_1
  N35: J2.#23, R4.Pin_1
  N36: J2.#24, R5.Pin_1
  N37: J2.GND#19, S2.leg0
  N38: R1.Pin_0, LED2.anode
  N39: R2.Pin_0, LED3.anode
  N40: R3.Pin_0, LED1.anode
  N41: R4.Pin_0, LED5.anode
  N42: R5.Pin_0, LED4.anode
  N43: R6.Pin_1, R7.Pin_0, S2.leg1

custom parts:
  T Cobbler Plus: The T-Cobbler Plus is an add on prototyping board from Adafruit specifically designed for the Raspberry Pi B+ that can break out all those tasty power, GPIO, I2C and SPI pins from the 40-pin header onto a solderless breadboard. This set will make "cobbling together" prototypes with the Pi super easy. The T-Cobbler Plus can plug into any solderless breadboard.
