# Fritzing sketch wiringPi-Button-Pin1 (saved by Fritzing 0.9.2b)
breadboards: 1

parts:
  S1 = Momentary Switch [package=tactile-pth]
  R2 = Resistor [tolerance=±5% resistance=1k package=THT]
  R1 = Resistor [tolerance=±5% resistance=10k package=THT]
  Raspberry_Pi1 = Raspberry Pi 2

nets:
  N1: S1.2, Raspberry_Pi1.3v3
  N2: S1.3, R2.Pin_1
  N3: S1.4, R1.Pin_0
  N4: R2.Pin_0, Raspberry_Pi1.GND
  N5: R1.Pin_1, Raspberry_Pi1.GPIO18
